# Fritzing sketch 06_one_dynamixel (saved by Fritzing 1.0.1rc)
breadboards: 1

parts:
  Mod1 = Raspberry Pi Pico
  S1 = Pushbutton [package="[THT]"]
  part = ttl2dxif [chip_label=IC]

nets:
  N1: Mod1.pin_3, Mod1.pin_8, Mod1.pin_13, Mod1.pin_18, Mod1.pin_23, Mod1.pin_28, Mod1.pin_33, Mod1.pin_38, Mod1.pin_42, part.connector3
  N2: Mod1.pin_15, part.connector2
  N3: Mod1.pin_16, part.connector1
  N4: Mod1.pin_21, S1.Pin_3, S1.Pin_4
  N5: Mod1.pin_36, S1.Pin_1, S1.Pin_2
  N6: Mod1.pin_40, part.connector0

notes:
  GP16 : pull down
  to dynamixel
  (右側は未配線で問題ない)

custom parts:
  Raspberry Pi Pico: Raspberry Pi Pico. Based around the RP2040 microcontroller the Pico is a low cost microcontroller device bringing Raspberry Pi quality, cost, and easy of use to the microcontroller space. Jan 2021, Split part in to two versions: tht (this one) and SMD. This one will drill holes for a .1 in header in pcb to allow plugging in the module as well as providing pads to solder the module to the top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
